# Fritzing sketch schematic (saved by Fritzing 0.9.3b)
breadboards: 1

parts:
  Part1 = Arduino Nano (Rev3.0)
  Part2 = Thumb Joystick
  Soft_Pot = SLIDER [part_number="SEN-08681 ROHS" package=slider]
  R1 = Resistor [tolerance=±5% resistance=220k package=THT]
  R2 = Resistor [tolerance=±5% resistance=10k package="0402 [SMD]"]
  R3 = Resistor [tolerance=±5% resistance=10k package="0402 [SMD]"]
  R4 = Resistor [tolerance=±5% resistance=10k package="0402 [SMD]"]
  SP1 = SPEAKER [package=pcb_mount_speaker]

nets:
  GND: Part1.GND, Part2.GND, Soft_Pot.A, R1.Pin_1, R2.Pin_1, R3.Pin_1, R4.Pin_1
  N1: Part1.D9, SP1.-
  N2: Part1.D10, SP1.+
  5V: Part1.5V, Part2.VCC, Soft_Pot.E
  N3: Part1.A4, Soft_Pot.S, R1.Pin_0
  N4: Part1.A3, Part2.SEL, R2.Pin_0
  N5: Part1.A2, Part2.HORZ, R3.Pin_0
  N6: Part1.A1, Part2.VERT, R4.Pin_0
